# Fritzing sketch mcp3008 (saved by Fritzing 0.9.3b)
breadboards: 1

parts:
  Raspberry_Pi_1 = Raspberry Pi 3 [part_number=RPI-3-V1.2]
  IC1 = MCP3008 8-channel 10-bit ADC [part_number=MCP3008]

nets:
  N1: Raspberry_Pi_1.3v3, IC1.no_name_yet#15, IC1.no_name_yet#16
  N2: Raspberry_Pi_1.GIPO10, IC1.no_name_yet#11
  N3: Raspberry_Pi_1.GIPO9, IC1.no_name_yet#12
  N4: Raspberry_Pi_1.GIPO11, IC1.no_name_yet#13
  N5: Raspberry_Pi_1.GND, IC1.no_name_yet#9, IC1.no_name_yet#14
  N6: Raspberry_Pi_1.GIPO8, IC1.no_name_yet#10
  N7: Raspberry_Pi_1.GIPO18, IC1.no_name_yet#1

notes:
  MCP3008 RPi 3 Test Platform
  ----------------------------------------
  Yellow: 3k8 13 <-> GPIO11 (SCLK)
  White: 3k8 12 <-> GPIO9 (MISO)
  Orange: 3k8 11 <-> GPIO10 (MOSI)
  Purple: 3k8 10 <-> GPIO8 (CE0)
  Pink: 3k8 A0 <-> GPIO18 (PWM)
