# Fritzing sketch dac_adc (saved by Fritzing 0.9.3b)
breadboards: 1

parts:
  Raspberry_Pi_1 = Raspberry Pi 3 [part_number=RPI-3-V1.2]
  ADC = Adafruit ADS1015 12Bit I2C ADC [part_number="Adafruit #1083"]
  R1 = Resistor [tolerance=±5% resistance=100 package="2010 [SMD]"]
  IC1 = IC, DIP package, 14 pins [chip_label=MCP4922]
  LED2 = LED - 3mm [color="Red (633nm)" package="3 mm [THT]"]
  R2 = Resistor [tolerance=±5% resistance=100 package="2010 [SMD]"]
  LED1 = LED - 3mm [color="Red (633nm)" package="3 mm [THT]"]

nets:
  3V3: Raspberry_Pi_1.3v3, Raspberry_Pi_1.3V3, ADC.VDD, IC1.pin1, IC1.pin11, IC1.pin13
  N1: Raspberry_Pi_1.GPIO2, ADC.SDA
  N2: Raspberry_Pi_1.GPIO3, ADC.SCL
  GND: Raspberry_Pi_1.GND, ADC.ADDR, ADC.GND, R1.Pin_0, IC1.pin8, IC1.pin12, R2.Pin_0
  N3: Raspberry_Pi_1.GPIO10, IC1.pin5
  N4: Raspberry_Pi_1.GPIO11, IC1.pin4
  N5: Raspberry_Pi_1.GPIO5, IC1.pin9
  N6: Raspberry_Pi_1.GPIO18, IC1.pin3
  N7: ADC.AIN1, IC1.pin10, LED1.anode
  N8: ADC.AIN0, IC1.pin14, LED2.anode
  N9: R1.Pin_1, LED1.cathode
  N10: LED2.cathode, R2.Pin_1

notes:
  Read DAC output with ADC
  ---------------------------------------
  - ADC model: ADS1015/1115 (i2c)
  - DAC model: MCP4922 (SPI)
  - Vdd == 3.3v
  ADC:
  ------
  purple: Pi SCL <-> ADC SCL
  yellow: Pi SDA <-> ADC SDA
  green: ADC ADDR <-> Gnd
  DAC:
  ------
  pink: ADC A0 <-> DAC A out (14) (LED0+)
  orange: ADC A1 <-> DAC B out (10) (LED1+)
  green: DAC LDAC (8) <-> Gnd
  brown: Pi GPIO 5 <-> DAC SHDN (9)
  lt blue: Pi MOSI <-> DAC SDI (5)
  blue: Pi: SCLK <-> DAC SCK (4)
  purple: Pi: GPIO 18 <-> DAC CS (3)
  DAC pins 2, 6, 7 == NC

custom parts:
  Adafruit ADS1015 12Bit I2C ADC: For microcontrollers without an analog-to-digital converter or when you want a higher-precision ADC, the ADS1015 provides 12-bit precision at 3300 samples/second over I2C. The chip can be configured as 4 single-ended input channels, or two differential channels. As a nice bonus, it even includes a programmable gain amplifier, up to x16, to help boost up smaller single/differential signals to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
