# Fritzing sketch adc_basic_example (saved by Fritzing 0.9.3b)
breadboards: 1

parts:
  Raspberry_Pi_1 = Raspberry Pi 3 [part_number=RPI-3-V1.2]
  ADC = Adafruit ADS1015 12Bit I2C ADC [part_number="Adafruit #1083"]
  LED1 = LED - 3mm [color="Red (633nm)" package="3 mm [THT]"]
  R1 = Resistor [tolerance=±5% resistance=220 package="0603 [SMD]"]

nets:
  3V3: Raspberry_Pi_1.3v3, ADC.VDD
  N1: Raspberry_Pi_1.GPIO2, ADC.SDA
  N2: Raspberry_Pi_1.GPIO3, ADC.SCL
  GND: Raspberry_Pi_1.GND, ADC.ADDR, ADC.GND, R1.Pin_0
  N3: Raspberry_Pi_1.GPIO18, ADC.AIN0, LED1.anode
  N4: LED1.cathode, R1.Pin_1

notes:
  Read variable output on an ADC
  ---------------------------------------
  - ADC model: ADS1015/1115
  - Vdd == 3.3v
  purple: Pi SCL <-> ADC SCL
  yellow: Pi SDA <-> ADC SDA
  pink: Pi GPIO 18 <-> LED+ (18==PWM)
  orange: ADC A0 <-> LED+
  green: ADC ADDR <-> Gnd
  As you adjust the output of GPIO pin 18 with PWM, the LED will change brightness intensity, and the variable output voltage of the pin will be picked up by pin A0 on the ADC.

custom parts:
  Adafruit ADS1015 12Bit I2C ADC: For microcontrollers without an analog-to-digital converter or when you want a higher-precision ADC, the ADS1015 provides 12-bit precision at 3300 samples/second over I2C. The chip can be configured as 4 single-ended input channels, or two differential channels. As a nice bonus, it even includes a programmable gain amplifier, up to x16, to help boost up smaller single/differential signals to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
