# Fritzing sketch dpot_adc (saved by Fritzing 0.9.3b)
breadboards: 1

parts:
  Raspberry_Pi_1 = Raspberry Pi 3 [part_number=RPI-3-V1.2]
  ADC = Adafruit ADS1015 12Bit I2C ADC [part_number="Adafruit #1083"]
  LED1 = LED - 3mm [color="Red (633nm)" package="3 mm [THT]"]
  U1 = MCP41xxx [package=so08]
  R1 = Resistor [tolerance=±5% resistance=100 package="2010 [SMD]"]

nets:
  3V3: Raspberry_Pi_1.3v3, ADC.VDD, U1.A, U1.VCC
  N1: Raspberry_Pi_1.GPIO2, ADC.SDA
  N2: Raspberry_Pi_1.GPIO3, ADC.SCL
  N3: Raspberry_Pi_1.GPIO10, U1.DI
  N4: Raspberry_Pi_1.GPIO11, U1.SCK
  GND: Raspberry_Pi_1.GND, ADC.ADDR, ADC.GND, U1.GND, U1.B, R1.Pin_0
  N5: Raspberry_Pi_1.GPIO18, U1.CS
  N6: ADC.AIN0, LED1.anode, U1.W
  N7: LED1.cathode, R1.Pin_1

notes:
  Read Digital Pot output with ADC
  ---------------------------------------
  - ADC model: ADS1015/1115
  - DigiPot model: MCP41010
  - Vdd == 3.3v
  purple: Pi SCL <-> ADC SCL
  yellow: Pi SDA <-> ADC SDA
  pink: Pi GPIO 18 <-> DPot CS (1)
  blue: ADC A0 <-> DPot Wiper (6) (LED+)
  lt blue: ADC MOSI <-> DPot IN
  orange: Pi SCLK <-> DPot CLK (2)
  green: ADC ADDR <-> Gnd

custom parts:
  Adafruit ADS1015 12Bit I2C ADC: For microcontrollers without an analog-to-digital converter or when you want a higher-precision ADC, the ADS1015 provides 12-bit precision at 3300 samples/second over I2C. The chip can be configured as 4 single-ended input channels, or two differential channels. As a nice bonus, it even includes a programmable gain amplifier, up to x16, to help boost up smaller single/differential signals to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
