# Fritzing sketch test_physical_setup (saved by Fritzing 0.9.3b)
breadboards: 1

parts:
  Raspberry_Pi_1 = Raspberry Pi 3 [part_number=RPI-3-V1.2]
  ADC = Adafruit ADS1015 12Bit I2C ADC [part_number="Adafruit #1083"]

nets:
  3V3: Raspberry_Pi_1.3v3, ADC.VDD
  N1: Raspberry_Pi_1.GPIO2, ADC.SDA
  N2: Raspberry_Pi_1.GPIO3, ADC.SCL
  GND: Raspberry_Pi_1.GND, ADC.ADDR, ADC.GND
  N3: Raspberry_Pi_1.GPIO18, ADC.AIN0

notes:
  WiringPi::API Testing Layout
  ---------------------------------------
  - ADC model: ADS1015/1115
  - Vdd == 3.3v
  purple: Pi SCL <-> ADC SCL
  yellow: Pi SDA <-> ADC SDA
  orange: Pi GPIO 18 <-> ADC A0
  green: ADC ADDR <-> Gnd

custom parts:
  Adafruit ADS1015 12Bit I2C ADC: For microcontrollers without an analog-to-digital converter or when you want a higher-precision ADC, the ADS1015 provides 12-bit precision at 3300 samples/second over I2C. The chip can be configured as 4 single-ended input channels, or two differential channels. As a nice bonus, it even includes a programmable gain amplifier, up to x16, to help boost up smaller single/differential signals to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
